# Fritzing sketch growmat (saved by Fritzing 0.9.2b)
circuit board: 8.46667cm x 5.64444cm

parts:
  Raspberry_Pi1 = Raspberry Pi 2
  J1 = Screw terminal - 2 pins [package=THT]
  J2 = RJ45 Jack [package=rj45-8]
  Power_plug1 = Power plug
  U1 = Voltage Regulator - 5V [package="TO220 [THT]"]
  JP1 = USB_MICROB_PLUG [package=micro-b-ra-smt]
  U2 = RELAY [package=relay-jzc]
  U3 = RELAY [package=relay-jzc]
  U4 = RELAY [package=relay-jzc]
  U5 = RELAY [package=relay-jzc]
  U6 = RELAY [package=relay-jzc]
  U7 = RELAY [package=relay-jzc]
  U8 = RELAY [package=relay-jzc]
  U9 = RELAY [package=relay-jzc]
  U10 = PCF8574 [package="DIP16 [THT]"]

nets:
  N1: Raspberry_Pi1.GPIO2, U10.SDA
  N2: Raspberry_Pi1.GPIO3, U10.SCL
  GND: Raspberry_Pi1.GND, U10.A0, U10.A1, U10.A3, U10.GND
  5V: Raspberry_Pi1.5V, U10.VCC
  N3: J1.pin1, J2.3
  N4: J1.pin2, J2.6
  N5: J2.4, J2.5, Power_plug1.VCC, U1.input_voltage
  GND_2: J2.7, J2.8, Power_plug1.GND, U1.GND, JP1.GND, U2.MAIN, U3.MAIN, U4.MAIN, U5.MAIN, U6.MAIN, U7.MAIN, U8.MAIN, U9.MAIN
  N6: U1.output_voltage, JP1.VCC
  N7: U2.COIL1, U10.P0
  N8: U4.COIL1, U10.P2
  N9: U5.COIL1, U10.P3
  N10: U6.COIL1, U10.P4
  N11: U7.COIL1, U10.P5
  N12: U8.COIL1, U10.P6
  N13: U9.COIL1, U10.P7

notes:
  WiFi
  RS485
  12VDC
  to Sensors
  Outputs
