# Fritzing sketch sensor (saved by Fritzing 0.9.2b)

parts:
  Součástka1 = Arduino Nano (Rev3.0) (ICSP)
  U2 = RS485 [package=so08]
  J3 = RJ45 Jack [package=rj45-8]
  U3 = RS485 [package=so08]  # not connected

nets:
  N1: Součástka1.D1/TX, U2.DI
  N2: Součástka1.D0/RX, U2.RO
  GND: Součástka1.GND, U2.GND, J3.7
  N3: Součástka1.D2, U2._RE, U2.DE
  N4: Součástka1.VIN, J3.5
  N5: U2.A, J3.3
  N6: U2.B, J3.6
