# Fritzing sketch input module rev0.1 (saved by Fritzing 0.9.2b)
circuit board: 7.04613cm x 17cm
breadboards: 1

parts:
  Part1 = Arduino Nano (Rev3.0)
  J2 = screw terminal, 3 pins
  R4 = Resistor [tolerance=±5% resistance=10k package=THT]
  R2 = Resistor [tolerance=±5% resistance=10k package=THT]
  J1 = screw terminal, 3 pins
  R3 = Resistor [tolerance=±5% resistance=10k package=THT]
  R9 = Resistor [tolerance=±5% resistance=10k package=THT]
  C4 = Ceramic Capacitor [capacitance=1µF package="100 mil [THT, multilayer]"]
  C5 = Ceramic Capacitor [capacitance=1µF package="100 mil [THT, multilayer]"]
  C6 = Ceramic Capacitor [capacitance=100nF package="100 mil [THT, multilayer]"]
  C7 = Ceramic Capacitor [capacitance=100nF package="100 mil [THT, multilayer]"]
  U3 = BNC [package=bnc]
  C3 = Ceramic Capacitor [capacitance=100nF package="100 mil [THT, multilayer]"]
  U2 = 555 Timer [package="DIP8 [THT]"]
  J6 = screw terminal, 8 pins
  R1 = Resistor [tolerance=±5% resistance=10k package=THT]
  J7 = male pin header, 6 pins [form="♂ (male)"]
  Component1 = RS485-Modul-Shield
  IC1 = Voltage Regulator [package=to220-igo]
  C9 = Tantalum Capacitor [capacitance=1μF package="100 mil [THT, tantalum]"]
  R10 = Resistor [tolerance=±5% resistance=390 package=THT]
  R12 = Resistor [tolerance=±5% resistance=390 package=THT]
  J8 = female pin header, 2 pins [form="♀ (female)"]
  J9 = female pin header, 2 pins [form="♀ (female)"]
  J10 = female pin header, 2 pins [form="♀ (female)"]
  J11 = female pin header, 2 pins [form="♀ (female)"]
  R11 = Resistor [tolerance=±5% resistance=220 package=THT]
  J5 = screw terminal, 8 pins
  C10 = Electrolytic Capacitor [capacitance=47µF voltage=20V package="200 mil [THT, electrolytic]"]
  C11 = Tantalum Capacitor [capacitance=1μF package="100 mil [THT, tantalum]"]
  C12 = Tantalum Capacitor [capacitance=1μF package="100 mil [THT, tantalum]"]
  R13 = Resistor [tolerance=±5% resistance=4.7k package=THT]
  J3 = screw terminal, 4 pins
  J4 = screw terminal, 4 pins
  R14 = Resistor [tolerance=±5% resistance=10k package=THT]
  R15 = Resistor [tolerance=±5% resistance=10k package=THT]

nets:
  N1: Part1.D1/TX, Component1.DI
  N2: Part1.D0/RX, Component1.RO
  GND: Part1.GND, J2.pin2, J1.pin2, C6.0, C7.0, C3.0, U2.Ground, J6.pin1, J6.pin2, J7.pin2, J7.pin3, Component1.GND, IC1.GND, C9.-, J9.pin2, J5.pin1, J5.pin2, C10.-, C11.-, C12.-, J3.pin2, J4.pin2
  N3: Part1.D2, Component1.RE, Component1.DE
  N4: Part1.D3, J1.pin3, R1.Pin_1
  N5: Part1.D4, J2.pin3, R2.Pin_1
  N6: Part1.D5, R3.Pin_1, J3.pin3
  N7: Part1.D6, R4.Pin_1, J4.pin3
  N8: Part1.D7, J7.pin6
  N9: Part1.D8, U2.Reset
  N10: Part1.D9, U2.Discharge, R13.Pin_1
  N11: Part1.VIN, J6.pin4, J6.pin5, IC1.IN, J5.pin4, J5.pin5, C10.+, C12.+
  5V: Part1.5V, Component1.VCC, J8.pin1
  N12: Part1.A3, J4.pin4, R14.Pin_1
  N13: Part1.A2, J3.pin4, R15.Pin_1
  N14: Part1.A1, J7.pin5
  N15: Part1.A0, J7.pin4
  N16: J2.pin1, R4.Pin_0, R2.Pin_0, J1.pin1, R3.Pin_0, C3.1, U2.Vcc_Supply_Voltage, R1.Pin_0, J7.pin1, IC1.OUT, C9.+, C11.+, R13.Pin_0, J3.pin1, J4.pin1, R14.Pin_0, R15.Pin_0
  N17: R9.Pin_0, C4.0, U2.Output
  N18: R9.Pin_1, C5.0, C6.1, U2.Trigger, U2.Threshold
  N19: C4.1, U3.OUT
  N20: C5.1, U3.GND
  N21: C7.1, U2.Control_Voltage
  N22: J6.pin3, Component1.B, J10.pin2, J5.pin3
  N23: J6.pin6, Component1.A, J11.pin2, J5.pin6
  N24: J6.pin7, J5.pin7
  N25: J6.pin8, J5.pin8
  N26: R10.Pin_0, J8.pin2
  N27: R10.Pin_1, J10.pin1, R11.Pin_0
  N28: R12.Pin_0, J11.pin1, R11.Pin_1
  N29: R12.Pin_1, J9.pin1

notes:
  G G D- 12V D+ x x
  D3
  D4
  5V G D6 A3
  D5 A2
  D7 A1 A0
  EC D8R D9
  Td Ta P G G 5V
  GROWMAT  0.1
  PH
  5V G

custom parts:
  RS485-Modul-Shield: Commercially available RS485 to RS232 TTL Module
