# Fritzing sketch output module rev0.1 (saved by Fritzing 0.9.2b)
circuit board: 7.04613cm x 13cm
breadboards: 1

parts:
  Part1 = Arduino Nano (Rev3.0)
  J6 = screw terminal, 8 pins
  Component1 = RS485-Modul-Shield
  IC1 = Voltage Regulator [package=to220-igo]
  C9 = Tantalum Capacitor [capacitance=1μF package="100 mil [THT, tantalum]"]
  R10 = Resistor [tolerance=±5% resistance=390 package=THT]
  R12 = Resistor [tolerance=±5% resistance=390 package=THT]
  J8 = female pin header, 2 pins [form="♀ (female)"]
  J9 = female pin header, 2 pins [form="♀ (female)"]
  J10 = female pin header, 2 pins [form="♀ (female)"]
  J11 = female pin header, 2 pins [form="♀ (female)"]
  R11 = Resistor [tolerance=±5% resistance=220 package=THT]
  J5 = screw terminal, 8 pins
  C10 = Electrolytic Capacitor [capacitance=47µF voltage=20V package="200 mil [THT, electrolytic]"]
  C11 = Tantalum Capacitor [capacitance=1μF package="100 mil [THT, tantalum]"]
  C12 = Tantalum Capacitor [capacitance=1μF package="100 mil [THT, tantalum]"]
  J12 = female pin header, 10 pins [form="♀ (female)"]
  J13 = female pin header, 2 pins [form="♀ (female)"]
  R13 = Resistor [tolerance=±5% resistance=33k package=THT]
  R14 = Resistor [tolerance=±5% resistance=33k package=THT]
  J14 = female pin header, 2 pins [form="♀ (female)"]
  J15 = female pin header, 2 pins [form="♀ (female)"]
  J18 = female pin header, 2 pins [form="♀ (female)"]
  J19 = female pin header, 2 pins [form="♀ (female)"]
  J20 = Screw terminal - 2 pins [package=THT]
  J21 = Screw terminal - 2 pins [package=THT]
  J22 = Screw terminal - 2 pins [package=THT]
  J23 = Screw terminal - 2 pins [package=THT]

nets:
  N1: Part1.D1/TX, Component1.DI
  N2: Part1.D0/RX, Component1.RO
  GND: Part1.GND, J6.pin1, J6.pin2, Component1.GND, IC1.GND, C9.-, J9.pin2, J5.pin1, J5.pin2, C10.-, C11.-, C12.-, J12.pin1, J13.pin2, J14.pin2, J15.pin2, J22.pin2, J23.pin2
  N3: Part1.D2, Component1.RE, Component1.DE
  N4: Part1.D3, J12.pin9
  N5: Part1.D4, J12.pin8
  N6: Part1.D5, J12.pin7
  N7: Part1.D6, J12.pin6
  N8: Part1.D7, J12.pin5
  N9: Part1.D8, J12.pin4
  N10: Part1.D9, J12.pin3, J23.pin1
  N11: Part1.D10, R14.Pin_0
  N12: Part1.D11/MOSI, R13.Pin_0
  N13: Part1.D12/MISO, J12.pin2, J22.pin1
  N14: Part1.VIN, J6.pin4, J6.pin5, IC1.IN, J5.pin4, J5.pin5, C10.+, C12.+
  5V: Part1.5V, Component1.VCC, J8.pin1, J12.pin10
  N15: J6.pin3, Component1.B, J10.pin2, J5.pin3
  N16: J6.pin6, Component1.A, J11.pin2, J5.pin6
  N17: J6.pin7, J5.pin7
  N18: J6.pin8, J5.pin8
  N19: IC1.OUT, C9.+, C11.+, J13.pin1
  N20: R10.Pin_0, J8.pin2
  N21: R10.Pin_1, J10.pin1, R11.Pin_0
  N22: R12.Pin_0, J11.pin1, R11.Pin_1
  N23: R12.Pin_1, J9.pin1
  N24: R13.Pin_1, J14.pin1
  N25: R14.Pin_1, J15.pin1
  N26: J18.pin1, J21.pin2
  N27: J18.pin2, J21.pin1
  N28: J19.pin1, J20.pin2
  N29: J19.pin2, J20.pin1

notes:
  G G D- 12V D+ x x
  GROWMAT 0.1
  +V G
  5V 3 4 5 6 7 8 9 12 G
  PWM 10
  PWM 11

custom parts:
  RS485-Modul-Shield: Commercially available RS485 to RS232 TTL Module
